// Digital circuit alu.dig as structural Verilog
module alu (
  input  n1,
  input  n2,
  input  n3,
  input  n4,
  input  n5,
  input  n6,
  input  n7,
  input  clock,
  input  start,
  input  op0,
  input  n0,
  input  op1,
  input  op2,
  output ac0,
  output ac1,
  output ac2,
  output ac3,
  output ac4,
  output ac5,
  output ac6,
  output ac7
);

  wire [7:0] div_out, mq_out, multiplexer_1_out, saidaNand, saidaXor, shiftd, shifte, somador8bits_1_c0,
       subtrator8bots_1_p16;

  somador8bits somador8bits_1 (
    .a0(ac0), .b0(n0), .a1(ac1), .b1(n1), .a2(ac2), .b2(n2), .a3(ac3), .b3(n3), .a4(ac4), .b4(n4), .a5(ac5),
    .b5(n5), .a6(ac6), .b6(n6), .a7(ac7), .b7(n7), .cin(1'b0), .c0(somador8bits_1_c0[0]),
    .c1(somador8bits_1_c0[1]), .c2(somador8bits_1_c0[2]), .c3(somador8bits_1_c0[3]),
    .c4(somador8bits_1_c0[4]), .c5(somador8bits_1_c0[5]), .c6(somador8bits_1_c0[6]), .c7(somador8bits_1_c0[7]));  // open: cout
  Multiplexer #(.Selector_Bits(3), .Bits(8)) multiplexer_1 (
    .sel({op2, op1, op0}), .in_0(somador8bits_1_c0), .in_1(subtrator8bots_1_p16), .in_2(saidaNand),
    .in_3(saidaXor), .in_4(shifte), .in_5(shiftd), .in_6(div_out), .out(multiplexer_1_out));  // open: in_7
  // subtrator8bots subtrator8bots_1: pin names not known; wires that end beside it: ac0, subtrator8bots_1_p16[7], n0, subtrator8bots_1_p16[6], ac1, subtrator8bots_1_p16[5], n1, subtrator8bots_1_p16[4], ac2, subtrator8bots_1_p16[3], n2, subtrator8bots_1_p16[2], ac3, subtrator8bots_1_p16[1], n3, subtrator8bots_1_p16[0], ac4, n4, n7, ac5, ac7, n5, n6, ac6
  Register #(.Bits(8)) AC (.D(multiplexer_1_out), .C(clock), .en(start), .Q({ac7, ac6, ac5, ac4, ac3, ac2, ac1, ac0}));
  Register #(.Bits(8)) MQ (.D(mq_out), .C(clock), .en(start));  // open: Q
  shift_left_8bits shift_left_8bits_1 (
    .a0(ac0), .a1(ac1), .a2(ac2), .a3(ac3), .a4(ac4), .a5(ac5), .a6(ac6), .a7(ac7), .c0(shifte[0]),
    .c1(shifte[1]), .c2(shifte[2]), .c3(shifte[3]), .c4(shifte[4]), .c5(shifte[5]), .c6(shifte[6]),
    .c7(shifte[7]));
  // divisor8bits divisor8bits_1: pin names not known; wires that end beside it: {ac7, ac6, ac5, ac4, ac3, ac2, ac1, ac0}, {n7, n6, n5, n4, n3, n2, n1, n0}, clock, start, div_out, mq_out
  sifht_right_8bits sifht_right_8bits_1 (
    .a7(ac7), .a6(ac6), .a5(ac5), .a4(ac4), .a3(ac3), .a2(ac2), .a1(ac1), .a0(ac0), .c0(shiftd[0]),
    .c1(shiftd[1]), .c2(shiftd[2]), .c3(shiftd[3]), .c4(shiftd[4]), .c5(shiftd[5]), .c6(shiftd[6]),
    .c7(shiftd[7]));
  xor_8bits xor_8bits_1 (
    .a0(ac0), .a1(ac1), .a2(ac2), .a3(ac3), .a4(ac4), .a5(ac5), .a6(ac6), .a7(ac7), .b0(n0), .b1(n1),
    .b2(n2), .b3(n3), .b4(n4), .b5(n5), .b6(n6), .b7(n7), .c0(saidaXor[0]), .c1(saidaXor[1]),
    .c2(saidaXor[2]), .c3(saidaXor[3]), .c4(saidaXor[4]), .c5(saidaXor[5]), .c6(saidaXor[6]), .c7(saidaXor[7]));
  nand_8bits nand_8bits_1 (
    .a0(ac0), .b0(n0), .a1(ac1), .b1(n1), .a2(ac2), .b2(n2), .a3(ac3), .b3(n3), .a4(ac4), .b4(n4), .a5(ac5),
    .b5(n5), .a6(ac6), .b6(n6), .a7(ac7), .b7(n7), .c0(saidaNand[0]), .c1(saidaNand[1]), .c2(saidaNand[2]),
    .c3(saidaNand[3]), .c4(saidaNand[4]), .c5(saidaNand[5]), .c6(saidaNand[6]), .c7(saidaNand[7]));

  // Other names for the same wires on the sheet: ac_div[7:0] = {ac7, ac6, ac5, ac4, ac3, ac2, ac1, ac0}; ao = ac0;
  //   sb0 = ac0; sd0 = ac0; se0 = ac0; xa0 = ac0; a1 = ac1; sb1 = ac1; sd1 = ac1; se1 = ac1; xa1 = ac1; a2 = ac2;
  //   sb2 = ac2; sd2 = ac2; se2 = ac2; xa2 = ac2; a3 = ac3; sb3 = ac3; sd3 = ac3; se3 = ac3; xa3 = ac3; a4 = ac4;
  //   sb4 = ac4; sd4 = ac4; se4 = ac4; xa4 = ac4; a5 = ac5; sb5 = ac5; sd5 = ac5; se5 = ac5; xa5 = ac5; a6 = ac6;
  //   sb6 = ac6; sd6 = ac6; se6 = ac6; xa6 = ac6; a7 = ac7; sb7 = ac7; sd7 = ac7; se7 = ac7; xa7 = ac7;
  //   clock_div = clock; start_div = start; b0 = n0; n_div[7:0] = {n7, n6, n5, n4, n3, n2, n1, n0}; nand0 = n0;
  //   sbn0 = n0; xb0 = n0; b1 = n1; nand1 = n1; sbn1 = n1; xb1 = n1; b2 = n2; nand2 = n2; sbn2 = n2; xb2 = n2;
  //   b3 = n3; nand3 = n3; sbn3 = n3; xb3 = n3; b4 = n4; nand4 = n4; sbn4 = n4; xb4 = n4; b5 = n5; nand5 = n5;
  //   sbn5 = n5; xb5 = n5; b6 = n6; nand6 = n6; sbn6 = n6; xb6 = n6; b7 = n7; nand7 = n7; sbn7 = n7; xb7 = n7
endmodule
