// Digital circuit alucerta.dig as structural Verilog
module alucerta (
  input  [7:0] N,
  input  En,
  input  Clk,
  input  [2:0] Op,
  output [7:0] Ac,
  output [7:0] Mq
);

  wire [7:0] Mul_plus_S, Mul_S, multiplexer_1_out, multiplexer_2_out, Nand, Quo, Rem, Sl, Sr, Sub, Sum, Xor;

  Mul #(.Bits(8)) mul_1 (.a(Ac), .b(N), .mul({Mul_plus_S, Mul_S}));
  BarrelShifter #(.Bits(8)) Esquerdo (.in(Ac), .shift(4'b0001), .out(Sl));
  assign Nand = ~(Ac & N);  // NAnd nand_1, 8 bits wide
  Add #(.Bits(8)) add_1 (.a(Ac), .b(N), .c_i(1'b0), .s(Sum));  // open: c_o
  BarrelShifter #(.Bits(8), .direction("right")) Direito (.in(Ac), .shift(4'b0001), .out(Sr));
  assign Xor = Ac ^ N;  // XOr xor_1, 8 bits wide
  Sub #(.Bits(8)) sub_1 (.a(Ac), .b(N), .c_i(1'b0), .s(Sub));  // open: c_o
  Div #(.Bits(8)) div_1 (.a(Ac), .b(N), .q(Quo), .r(Rem));
  Multiplexer #(.Selector_Bits(3), .Bits(8)) multiplexer_1 (
    .sel(Op), .in_0(Sum), .in_1(Sub), .in_2(Mul_S), .in_3(Rem), .in_4(Nand), .in_5(Xor), .in_6(Sl),
    .in_7(Sr), .out(multiplexer_1_out));
  Multiplexer #(.Selector_Bits(3), .Bits(8)) multiplexer_2 (
    .sel(Op), .in_0(Mq), .in_1(Mq), .in_2(Mul_plus_S), .in_3(Quo), .in_4(Mq), .in_5(Mq), .in_6(Mq),
    .in_7(Mq), .out(multiplexer_2_out));
  Register #(.Bits(8)) register_1 (.D(multiplexer_1_out), .C(Clk), .en(En), .Q(Ac));
  Register #(.Bits(8)) register_2 (.D(multiplexer_2_out), .C(Clk), .en(En), .Q(Mq));
endmodule
