// Digital circuit cpu.dig as structural Verilog
module cpu (
  input  Clock,
  output [7:0] AC,
  output [7:0] MQ
);

  wire Deq, Qe;
  wire [2:0] register_1_q_2;
  wire [7:0] pc_1_addr, register_1_q;
  wire [10:0] rom_1_d;

  pc pc_1 (.Clk(Clock), .En(Deq), .Addr(pc_1_addr));
  ROM #(.AddrBits(8), .Bits(11)) rom_1 (.A(pc_1_addr), .sel(Qe), .D(rom_1_d));
  D_FF d_ff_1 (.D(Qe), .C(Clock), .Q(Deq), .nQ(Qe));
  Register #(.Bits(11)) register_1 (.D(rom_1_d), .C(Clock), .en(Qe), .Q({register_1_q_2, register_1_q}));
  alucerta alucerta_1 (.N(register_1_q), .En(Deq), .Clk(Clock), .Op(register_1_q_2), .Ac(AC), .Mq(MQ));

  // Notes on the sheet:
  //   contents of rom_1 (hex, n*v repeats v):
  //   2,302
endmodule
