// Digital circuit nand_8bits.dig as structural Verilog
module nand_8bits (
  input  a0,
  input  b0,
  input  a1,
  input  b1,
  input  a2,
  input  b2,
  input  a3,
  input  b3,
  input  a4,
  input  b4,
  input  a5,
  input  b5,
  input  a6,
  input  b6,
  input  a7,
  input  b7,
  output c0,
  output c1,
  output c2,
  output c3,
  output c4,
  output c5,
  output c6,
  output c7
);

  nand nand_1 (c0, a0, b0);
  nand nand_2 (c1, a1, b1);
  nand nand_3 (c2, a2, b2);
  nand nand_4 (c3, a3, b3);
  nand nand_5 (c4, a4, b4);
  nand nand_6 (c5, a5, b5);
  nand nand_7 (c6, a6, b6);
  nand nand_8 (c7, a7, b7);
endmodule
