// Digital circuit pc.dig as structural Verilog
module pc (
  input  Clk,
  input  En,
  output [7:0] Addr
);

  wire [7:0] add_1_s;

  Register #(.Bits(8)) register_1 (.D(add_1_s), .C(Clk), .en(En), .Q(Addr));
  Add #(.Bits(8)) add_1 (.a(Addr), .b(8'h1), .c_i(1'b0), .s(add_1_s));  // open: c_o

  // Other names for the same wires on the sheet: ad[7:0] = Addr
endmodule
