// Digital circuit somador8bits.dig as structural Verilog
module somador8bits (
  input  a0,
  input  b0,
  input  a1,
  input  b1,
  input  a2,
  input  b2,
  input  a3,
  input  b3,
  input  a4,
  input  b4,
  input  a5,
  input  b5,
  input  a6,
  input  b6,
  input  a7,
  input  b7,
  input  cin,
  output c0,
  output c1,
  output c2,
  output c3,
  output c4,
  output c5,
  output c6,
  output c7,
  output cout
);

  wire s0, s1, s2, s3, s4, s5, s6;

  // somador1bit somador1bit_1: pin names not known; wires that end beside it: cin, b0, s0, a0, c0
  // somador1bit somador1bit_2: pin names not known; wires that end beside it: s0, b1, s1, a1, c1
  // somador1bit somador1bit_3: pin names not known; wires that end beside it: s1, b2, s2, a2, c2
  // somador1bit somador1bit_4: pin names not known; wires that end beside it: s2, b3, s3, a3, c3
  // somador1bit somador1bit_5: pin names not known; wires that end beside it: s3, b4, s4, a4, c4
  // somador1bit somador1bit_6: pin names not known; wires that end beside it: s4, b5, s5, a5, c5
  // somador1bit somador1bit_7: pin names not known; wires that end beside it: s5, b6, s6, a6, c6
  // somador1bit somador1bit_8: pin names not known; wires that end beside it: s6, b7, cout, a7, c7
endmodule
