// Digital circuit xor_8bits.dig as structural Verilog
module xor_8bits (
  input  a0,
  input  a1,
  input  a2,
  input  a3,
  input  a4,
  input  a5,
  input  a6,
  input  a7,
  input  b0,
  input  b1,
  input  b2,
  input  b3,
  input  b4,
  input  b5,
  input  b6,
  input  b7,
  output c0,
  output c1,
  output c2,
  output c3,
  output c4,
  output c5,
  output c6,
  output c7
);

  xor xor_1 (c6, a6, b6);
  xor xor_2 (c7, a7, b7);
  xor xor_3 (c0, a0, b0);
  xor xor_4 (c1, a1, b1);
  xor xor_5 (c2, a2, b2);
  xor xor_6 (c3, a3, b3);
  xor xor_7 (c4, a4, b4);
  xor xor_8 (c5, a5, b5);
endmodule
